# Fritzing sketch 3.2C Sketch (saved by Fritzing 1.0.2b)
breadboards: 1

parts:
  Part1 = BH1750
  M1 = Arduino Nano 33 IOT-smd

nets:
  N1: Part1.VCC, M1.pin_2
  N2: Part1.GND, M1.pin_14, M1.pin_19
  N3: Part1.SCL, M1.pin_9
  N4: Part1.SDA, M1.pin_8
  N5: M1.pin_13, M1.pin_18

custom parts:
  BH1750: Light Sensor
  Arduino Nano 33 IOT-smd: The Arduino Nano 33 IoT is the easiest and cheapest point of entry to enhance existing devices (and creating new ones) to be part of the IoT and designing pico-network applications. Whether you are looking at building a sensor network connected to your office or home router, or if you want to create a BLE device sending data to a cellphone, the Nano 33 IoT is your one-stop-solution for many of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
